// Logisim project DSDPROJ.circ as structural Verilog: 19 circuits, main circuit Main
module TrafficControllerMain (
  input  E,
  input  X,
  input  in_3,
  input  R,
  output LE_0,
  output LE_1,
  output LX_0,
  output LX_1,
  output C_0,
  output C_1,
  output C_2,
  output C_3
);

  wire [5:0] register_1_q, s5circuitprime_1_o;

  s0CircuitPrime s0circuitprime_1 (
    .s0(register_1_q[5]), .s1(register_1_q[4]), .s2(register_1_q[3]), .s3(register_1_q[2]),
    .s4(register_1_q[1]), .s5(register_1_q[0]), .E(E), .X(X), .O(s5circuitprime_1_o[5]));
  s1CircuitPrime s1circuitprime_1 (
    .s0(register_1_q[5]), .s1(register_1_q[4]), .s2(register_1_q[3]), .s3(register_1_q[2]),
    .s4(register_1_q[1]), .s5(register_1_q[0]), .E(E), .X(X), .O(s5circuitprime_1_o[4]));
  s2CircuitPrime s2circuitprime_1 (
    .s0(register_1_q[5]), .s1(register_1_q[4]), .s2(register_1_q[3]), .s3(register_1_q[2]),
    .s4(register_1_q[1]), .s5(register_1_q[0]), .E(E), .X(X), .O(s5circuitprime_1_o[3]));
  s3CircuitPrime s3circuitprime_1 (
    .s0(register_1_q[5]), .s1(register_1_q[4]), .s2(register_1_q[3]), .s3(register_1_q[2]),
    .s4(register_1_q[1]), .s5(register_1_q[0]), .E(E), .X(X), .O(s5circuitprime_1_o[2]));
  s4CircuitPrime s4circuitprime_1 (
    .s0(register_1_q[5]), .s1(register_1_q[4]), .s2(register_1_q[3]), .s3(register_1_q[2]),
    .s4(register_1_q[1]), .s5(register_1_q[0]), .E(E), .X(X), .O(s5circuitprime_1_o[1]));
  s5CircuitPrime s5circuitprime_1 (
    .s0(register_1_q[5]), .s1(register_1_q[4]), .s2(register_1_q[3]), .s3(register_1_q[2]),
    .s4(register_1_q[1]), .s5(register_1_q[0]), .E(E), .X(X), .O(s5circuitprime_1_o[0]));
  Register #(.width(6)) register_1 (.D(s5circuitprime_1_o), .clk(in_3), .Q(register_1_q), .clr(R));  // open: en
  LE0 LE00 (
    .s0(register_1_q[5]), .s1(register_1_q[4]), .s2(register_1_q[3]), .s3(register_1_q[2]),
    .s4(register_1_q[1]), .s5(register_1_q[0]), .O(LE_0));
  LE1 le1_1 (
    .s0(register_1_q[5]), .s1(register_1_q[4]), .s2(register_1_q[3]), .s3(register_1_q[2]),
    .s4(register_1_q[1]), .s5(register_1_q[0]), .O(LE_1));
  LX0 lx0_1 (
    .s0(register_1_q[5]), .s1(register_1_q[4]), .s2(register_1_q[3]), .s3(register_1_q[2]),
    .s4(register_1_q[1]), .s5(register_1_q[0]), .O(LX_0));
  LX1 lx1_1 (
    .s0(register_1_q[5]), .s1(register_1_q[4]), .s2(register_1_q[3]), .s3(register_1_q[2]),
    .s4(register_1_q[1]), .s5(register_1_q[0]), .O(LX_1));
  C0 c0_1 (
    .s0(register_1_q[5]), .s1(register_1_q[4]), .s2(register_1_q[3]), .s3(register_1_q[2]),
    .s4(register_1_q[1]), .s5(register_1_q[0]), .O(C_0));
  C1 c1_1 (
    .s0(register_1_q[5]), .s1(register_1_q[4]), .s2(register_1_q[3]), .s3(register_1_q[2]),
    .s4(register_1_q[1]), .s5(register_1_q[0]), .O(C_1));
  C2 c2_1 (
    .s0(register_1_q[5]), .s1(register_1_q[4]), .s2(register_1_q[3]), .s3(register_1_q[2]),
    .s4(register_1_q[1]), .s5(register_1_q[0]), .O(C_2));
  C3 c3_1 (
    .s0(register_1_q[5]), .s1(register_1_q[4]), .s2(register_1_q[3]), .s3(register_1_q[2]),
    .s4(register_1_q[1]), .s5(register_1_q[0]), .O(C_3));
endmodule

module s0CircuitPrime (
  input  s0,
  input  s1,
  input  s2,
  input  s3,
  input  s4,
  input  s5,
  input  E,
  input  X,
  output O
);

  wire and_1_out, and_2_out, and_3_out, and_4_out, and_5_out, and_6_out, not_1_out, not_2_out, not_3_out,
       not_4_out, not_5_out;

  not not_1 (not_1_out, s1);
  not not_2 (not_2_out, s2);
  not not_3 (not_3_out, s3);
  not not_4 (not_4_out, s4);
  not not_5 (not_5_out, X);
  and and_1 (and_1_out, not_1_out, not_2_out, s3, s4, s5, X);
  and and_2 (and_2_out, not_1_out, s2, not_3_out, not_4_out, X);
  and and_3 (and_3_out, s1, s2, s3, s4, s5);
  and and_4 (and_4_out, s0, not_4_out, not_5_out);
  and and_5 (and_5_out, s0, s5);
  and and_6 (and_6_out, s0, s3, not_4_out);
  or or_1 (O, and_1_out, and_2_out, and_3_out, and_4_out, and_5_out, and_6_out);
endmodule

module s1CircuitPrime (
  input  s0,
  input  s1,
  input  s2,
  input  s3,
  input  s4,
  input  s5,
  input  E,
  input  X,
  output O
);

  wire and_1_out, and_2_out, and_3_out, and_4_out, and_5_out, and_6_out, and_7_out, and_8_out, and_9_out,
       not_1_out, not_2_out, not_3_out, not_4_out, not_5_out, not_6_out, not_7_out;

  not not_1 (not_1_out, s0);
  not not_2 (not_2_out, s1);
  not not_3 (not_3_out, s2);
  not not_4 (not_4_out, s3);
  not not_5 (not_5_out, s4);
  not not_6 (not_6_out, s5);
  not not_7 (not_7_out, X);
  and and_1 (and_1_out, not_1_out, not_3_out, not_4_out, s4, s5, X);
  and and_2 (and_2_out, not_1_out, not_2_out, not_3_out, s3, not_6_out, X);
  and and_3 (and_3_out, not_1_out, not_3_out, s3, not_5_out, X);
  and and_4 (and_4_out, not_2_out, s2, s3, s5, X);
  and and_5 (and_5_out, s1, not_5_out, not_7_out);
  and and_6 (and_6_out, s1, not_3_out, s5);
  and and_7 (and_7_out, s1, not_4_out, s5);
  and and_8 (and_8_out, s1, s2, not_5_out);
  and and_9 (and_9_out, s0, not_3_out, not_4_out, not_5_out, X);
  or or_1 (O, and_1_out, and_2_out, and_3_out, and_4_out, and_5_out, and_6_out, and_7_out, and_8_out, and_9_out);
endmodule

module s2CircuitPrime (
  input  s0,
  input  s1,
  input  s2,
  input  s3,
  input  s4,
  input  s5,
  input  E,
  input  X,
  output O
);

  wire and_1_out, and_2_out, and_3_out, and_4_out, and_5_out, and_6_out, and_7_out, and_8_out, and_9_out,
       and_10_out, and_11_out, and_12_out, and_13_out, and_14_out, not_1_out, not_2_out, not_3_out,
       not_4_out, not_5_out, not_6_out, not_7_out;

  not not_1 (not_1_out, s0);
  not not_2 (not_2_out, s1);
  not not_3 (not_3_out, s2);
  not not_4 (not_4_out, s3);
  not not_5 (not_5_out, s4);
  not not_6 (not_6_out, s5);
  not not_7 (not_7_out, X);
  and and_1 (and_1_out, not_5_out, s5, X);
  and and_2 (and_2_out, not_1_out, not_2_out, not_3_out, s4, not_6_out, X);
  and and_3 (and_3_out, s3, s4, s5, E, not_7_out);
  and and_4 (and_4_out, s2, not_5_out, not_7_out);
  and and_5 (and_5_out, s2, not_4_out, s5);
  and and_6 (and_6_out, s2, s5, not_7_out);
  and and_7 (and_7_out, s2, s3, not_5_out);
  and and_8 (and_8_out, s1, not_3_out, not_4_out, not_5_out, X);
  and and_9 (and_9_out, s1, not_3_out, s3, s5, X);
  and and_10 (and_10_out, s0, not_3_out, not_4_out, not_5_out, X);
  and and_11 (and_11_out, s0, s3, s5, X);
  and and_12 (and_12_out, s0, s3, s4, E);
  and and_13 (and_13_out, s0, s2, not_7_out);
  and and_14 (and_14_out, s0, s2, s4);
  or or_1 (O, and_1_out, and_2_out, and_3_out, and_4_out, and_5_out, and_6_out, and_7_out, and_8_out, and_9_out, and_10_out, and_11_out, and_12_out, and_13_out, and_14_out);
endmodule

module s3CircuitPrime (
  input  s0,
  input  s1,
  input  s2,
  input  s3,
  input  s4,
  input  s5,
  input  E,
  input  X,
  output O
);

  wire and_1_out, and_2_out, and_3_out, and_4_out, and_5_out, and_6_out, and_7_out, and_8_out, and_9_out,
       and_10_out, and_11_out, and_12_out, and_13_out, and_14_out, and_15_out, not_1_out, not_2_out,
       not_3_out, not_4_out, not_5_out, not_6_out, not_7_out, not_8_out;

  not not_1 (not_1_out, s0);
  not not_2 (not_2_out, s1);
  not not_3 (not_3_out, s2);
  not not_4 (not_4_out, s3);
  not not_5 (not_5_out, s4);
  not not_6 (not_6_out, s5);
  not not_7 (not_7_out, E);
  not not_8 (not_8_out, X);
  and and_1 (and_1_out, not_1_out, not_2_out, not_3_out, s4, not_6_out, X);
  and and_2 (and_2_out, not_4_out, s4, s5, E, not_8_out);
  and and_3 (and_3_out, not_1_out, not_2_out, not_3_out, s3, not_6_out);
  and and_4 (and_4_out, s3, not_5_out, not_8_out);
  and and_5 (and_5_out, s3, s5, not_7_out, not_8_out);
  and and_6 (and_6_out, not_1_out, not_3_out, s3, s4, not_6_out, E);
  and and_7 (and_7_out, s2, not_4_out, not_5_out, not_6_out, X);
  and and_8 (and_8_out, s2, not_4_out, s4, s5);
  and and_9 (and_9_out, s1, not_4_out, not_5_out, X);
  and and_10 (and_10_out, s1, not_4_out, s5, X);
  and and_11 (and_11_out, s1, s2, s4, not_6_out);
  and and_12 (and_12_out, s0, not_3_out, not_4_out, X);
  and and_13 (and_13_out, s0, not_3_out, not_4_out, s4);
  and and_14 (and_14_out, s0, not_3_out, s4, not_6_out, not_7_out);
  and and_15 (and_15_out, s0, not_3_out, s4, not_7_out, not_8_out);
  or or_1 (O, and_1_out, and_2_out, and_3_out, and_4_out, and_5_out, and_6_out, and_7_out, and_8_out, and_9_out, and_10_out, and_11_out, and_12_out, and_13_out, and_14_out, and_15_out);
endmodule

module s4CircuitPrime (
  input  s0,
  input  s1,
  input  s2,
  input  s3,
  input  s4,
  input  s5,
  input  E,
  input  X,
  output O
);

  wire and_1_out, and_2_out, and_3_out, and_4_out, and_5_out, and_6_out, and_7_out, and_8_out, and_9_out,
       and_10_out, and_11_out, and_12_out, and_13_out, and_14_out, and_15_out, and_16_out, and_17_out,
       not_1_out, not_2_out, not_3_out, not_4_out, not_5_out, not_6_out, not_7_out, not_8_out;

  not not_1 (not_1_out, s0);
  not not_2 (not_2_out, s1);
  not not_3 (not_3_out, s2);
  not not_4 (not_4_out, s3);
  not not_5 (not_5_out, s4);
  not not_6 (not_6_out, s5);
  not not_7 (not_7_out, E);
  not not_8 (not_8_out, X);
  and and_1 (and_1_out, not_1_out, not_2_out, not_3_out, s5, X);
  and and_2 (and_2_out, not_3_out, not_5_out, s5, E);
  and and_3 (and_3_out, not_1_out, not_2_out, not_3_out, s4, not_6_out);
  and and_4 (and_4_out, not_1_out, not_2_out, not_4_out, s4, not_7_out, not_8_out);
  and and_5 (and_5_out, not_3_out, s4, not_6_out, not_7_out);
  and and_6 (and_6_out, not_1_out, not_2_out, not_3_out, s4, X);
  and and_7 (and_7_out, s4, s5, not_7_out, not_8_out);
  and and_8 (and_8_out, not_1_out, not_2_out, not_3_out, s3, X);
  and and_9 (and_9_out, not_1_out, not_2_out, s3, E, X);
  and and_10 (and_10_out, s3, not_5_out, s5, E);
  and and_11 (and_11_out, not_1_out, not_2_out, s3, s4, not_6_out, E);
  and and_12 (and_12_out, not_1_out, not_2_out, s2, not_5_out, X);
  and and_13 (and_13_out, s2, s3, s4, E);
  and and_14 (and_14_out, s1, s5, E);
  and and_15 (and_15_out, s1, not_3_out, not_4_out, s4, E);
  and and_16 (and_16_out, s0, s5, E);
  and and_17 (and_17_out, s0, not_3_out, not_4_out, s4, E);
  or or_1 (O, and_1_out, and_2_out, and_3_out, and_4_out, and_5_out, and_6_out, and_7_out, and_8_out, and_9_out, and_10_out, and_11_out, and_12_out, and_13_out, and_14_out, and_15_out, and_16_out, and_17_out);
endmodule

module s5CircuitPrime (
  input  s0,
  input  s1,
  input  s2,
  input  s3,
  input  s4,
  input  s5,
  input  E,
  input  X,
  output O
);

  wire and_1_out, and_2_out, and_3_out, and_4_out, and_5_out, and_6_out, and_7_out, and_8_out, and_9_out,
       and_10_out, and_11_out, and_12_out, and_13_out, and_14_out, and_15_out, not_1_out, not_2_out,
       not_3_out, not_4_out, not_5_out, not_6_out, not_7_out, not_8_out;

  not not_1 (not_1_out, s0);
  not not_2 (not_2_out, s1);
  not not_3 (not_3_out, s2);
  not not_4 (not_4_out, s3);
  not not_5 (not_5_out, s4);
  not not_6 (not_6_out, s5);
  not not_7 (not_7_out, E);
  not not_8 (not_8_out, X);
  and and_1 (and_1_out, not_1_out, not_2_out, not_3_out, not_6_out, E);
  and and_2 (and_2_out, not_4_out, not_6_out, E, not_8_out);
  and and_3 (and_3_out, not_5_out, not_6_out, E, not_8_out);
  and and_4 (and_4_out, s5, not_7_out, not_8_out);
  and and_5 (and_5_out, not_5_out, s5, X);
  and and_6 (and_6_out, not_1_out, not_2_out, not_3_out, s4, X);
  and and_7 (and_7_out, not_1_out, not_2_out, not_3_out, s3, X);
  and and_8 (and_8_out, s3, s4, not_6_out, not_7_out, X);
  and and_9 (and_9_out, not_1_out, not_2_out, s2, not_4_out, not_5_out, X);
  and and_10 (and_10_out, not_1_out, not_2_out, s2, not_4_out, not_5_out, s5);
  and and_11 (and_11_out, s2, s3, s4, not_7_out, not_8_out);
  and and_12 (and_12_out, s1, not_4_out, s4, E);
  and and_13 (and_13_out, s1, s3, s4, not_6_out, not_7_out);
  and and_14 (and_14_out, s0, not_4_out, s4, E);
  and and_15 (and_15_out, s0, s3, s4, not_6_out, not_7_out);
  or or_1 (O, and_1_out, and_2_out, and_3_out, and_4_out, and_5_out, and_6_out, and_7_out, and_8_out, and_9_out, and_10_out, and_11_out, and_12_out, and_13_out, and_14_out, and_15_out);
endmodule

module LE0 (
  input  s0,
  input  s1,
  input  s2,
  input  s3,
  input  s4,
  input  s5,
  output O
);

  wire and_1_out, and_2_out, and_3_out, and_4_out, not_1_out, not_2_out, not_3_out, not_4_out, not_5_out;

  not not_1 (not_1_out, s0);
  not not_2 (not_2_out, s1);
  not not_3 (not_3_out, s3);
  not not_4 (not_4_out, s4);
  not not_5 (not_5_out, s5);
  and and_1 (and_1_out, not_1_out, not_2_out, s2, not_3_out, s4, not_5_out);
  and and_2 (and_2_out, s2, s3, not_4_out);
  and and_3 (and_3_out, s1, not_4_out);
  and and_4 (and_4_out, s0, not_4_out);
  or or_1 (O, and_1_out, and_2_out, and_3_out, and_4_out);
endmodule

module LE1 (
  input  s0,
  input  s1,
  input  s2,
  input  s3,
  input  s4,
  input  s5,
  output O
);

  wire and_1_out, and_2_out, and_3_out;

  and and_1 (and_1_out, s2, s4, s5);
  and and_2 (and_2_out, s1, s4, s5);
  and and_3 (and_3_out, s0, s4, s5);
  or or_1 (O, and_1_out, and_2_out, and_3_out);
endmodule

module LX0 (
  input  s0,
  input  s1,
  input  s2,
  input  s3,
  input  s4,
  input  s5,
  output O
);

  wire and_1_out, and_2_out, and_3_out, and_4_out, and_5_out, and_6_out, and_7_out, not_1_out, not_2_out,
       not_3_out, not_4_out, not_5_out;

  not not_1 (not_1_out, s0);
  not not_2 (not_2_out, s1);
  not not_3 (not_3_out, s2);
  not not_4 (not_4_out, s3);
  not not_5 (not_5_out, s4);
  and and_1 (and_1_out, not_1_out, not_2_out, not_3_out);
  and and_2 (and_2_out, not_1_out, not_2_out, not_4_out, not_5_out);
  and and_3 (and_3_out, not_1_out, not_2_out, not_4_out, s5);
  and and_4 (and_4_out, s4, s5);
  and and_5 (and_5_out, s3, s4);
  and and_6 (and_6_out, s1, s4);
  and and_7 (and_7_out, s0, s4);
  or or_1 (O, and_1_out, and_2_out, and_3_out, and_4_out, and_5_out, and_6_out, and_7_out);
endmodule

module LX1 (
  input  s0,
  input  s1,
  input  s2,
  input  s3,
  input  s4,
  input  s5,
  output O
);

  wire and_1_out, and_2_out, and_3_out, and_4_out, not_1_out, not_2_out, not_3_out, not_4_out, not_5_out;

  not not_1 (not_1_out, s0);
  not not_2 (not_2_out, s1);
  not not_3 (not_3_out, s3);
  not not_4 (not_4_out, s4);
  not not_5 (not_5_out, s5);
  and and_1 (and_1_out, not_1_out, not_2_out, s2, not_3_out, s4, not_5_out);
  and and_2 (and_2_out, s2, s3, not_4_out, s5);
  and and_3 (and_3_out, s1, not_4_out, s5);
  and and_4 (and_4_out, s0, not_4_out, s5);
  or or_1 (O, and_1_out, and_2_out, and_3_out, and_4_out);
endmodule

module Main (
  input  E,
  input  X,
  input  R
);

  wire clock_1_out, leselector_1_green, leselector_1_red, leselector_1_yellow, lxselector_1_green,
       lxselector_1_red, lxselector_1_yellow, sevenseg_1_a, sevenseg_1_b, sevenseg_1_c, sevenseg_1_d,
       sevenseg_1_e, sevenseg_1_f, sevenseg_1_g, trafficcontrollermain_1_c_0, trafficcontrollermain_1_c_1,
       trafficcontrollermain_1_c_2, trafficcontrollermain_1_c_3, trafficcontrollermain_1_le_0,
       trafficcontrollermain_1_le_1, trafficcontrollermain_1_lx_0, trafficcontrollermain_1_lx_1;

  Clock clock_1 (.out(clock_1_out));
  TrafficControllerMain trafficcontrollermain_1 (
    .E(E), .X(X), .in_3(clock_1_out), .R(R), .LE_0(trafficcontrollermain_1_le_0),
    .LE_1(trafficcontrollermain_1_le_1), .LX_0(trafficcontrollermain_1_lx_0),
    .LX_1(trafficcontrollermain_1_lx_1), .C_0(trafficcontrollermain_1_c_0),
    .C_1(trafficcontrollermain_1_c_1), .C_2(trafficcontrollermain_1_c_2), .C_3(trafficcontrollermain_1_c_3));
  LED led_1 (.in(leselector_1_red));
  LESelector leselector_1 (
    .LE0(trafficcontrollermain_1_le_0), .LE1(trafficcontrollermain_1_le_1), .RED(leselector_1_red),
    .YELLOW(leselector_1_yellow), .GREEN(leselector_1_green));
  LED led_2 (.in(leselector_1_yellow));
  LED led_3 (.in(leselector_1_green));
  LED led_4 (.in(lxselector_1_red));
  LXSelector lxselector_1 (
    .LX0(trafficcontrollermain_1_lx_0), .LX1(trafficcontrollermain_1_lx_1), .RED(lxselector_1_red),
    .YELLOW(lxselector_1_yellow), .GREEN(lxselector_1_green));
  LED led_5 (.in(lxselector_1_yellow));
  LED led_6 (.in(lxselector_1_green));
  SevenSeg sevenseg_1 (
    .C_0(trafficcontrollermain_1_c_3), .C_1(trafficcontrollermain_1_c_2), .C_2(trafficcontrollermain_1_c_1),
    .C_3(trafficcontrollermain_1_c_0), .A(sevenseg_1_a), .B(sevenseg_1_b), .C(sevenseg_1_c),
    .D(sevenseg_1_d), .E(sevenseg_1_e), .F(sevenseg_1_f), .G(sevenseg_1_g));
  _7_Segment_Display u_7_segment_display_1 (
    .g(sevenseg_1_g), .f(sevenseg_1_f), .a(sevenseg_1_a), .b(sevenseg_1_b), .e(sevenseg_1_e),
    .d(sevenseg_1_d), .c(sevenseg_1_c));  // open: dp
endmodule

module C0 (
  input  s0,
  input  s1,
  input  s2,
  input  s3,
  input  s4,
  input  s5,
  output O
);

  wire and_1_out, and_2_out, and_3_out, not_1_out, not_2_out, not_3_out;

  not not_1 (not_1_out, s1);
  not not_2 (not_2_out, s3);
  not not_3 (not_3_out, s4);
  and and_1 (and_1_out, not_1_out, s2, not_2_out, not_3_out);
  and and_2 (and_2_out, s0, s3, s4, s5);
  and and_3 (and_3_out, s0, s2);
  or or_1 (O, and_1_out, and_2_out, and_3_out);
endmodule

module C1 (
  input  s0,
  input  s1,
  input  s2,
  input  s3,
  input  s4,
  input  s5,
  output O
);

  wire and_1_out, and_2_out, and_3_out, and_4_out, and_5_out, and_6_out, not_1_out, not_2_out, not_3_out,
       not_4_out, not_5_out, not_6_out;

  not not_1 (not_1_out, s0);
  not not_2 (not_2_out, s1);
  not not_3 (not_3_out, s2);
  not not_4 (not_4_out, s3);
  not not_5 (not_5_out, s4);
  not not_6 (not_6_out, s5);
  and and_1 (and_1_out, not_1_out, not_2_out, not_3_out, s3);
  and and_2 (and_2_out, not_1_out, not_3_out, s3, s4, s5);
  and and_3 (and_3_out, s1, s2);
  and and_4 (and_4_out, s0, not_3_out, not_4_out);
  and and_5 (and_5_out, s0, not_3_out, not_6_out);
  and and_6 (and_6_out, s0, s3, not_5_out, s5);
  or or_1 (O, and_1_out, and_2_out, and_3_out, and_4_out, and_5_out, and_6_out);
endmodule

module C2 (
  input  s0,
  input  s1,
  input  s2,
  input  s3,
  input  s4,
  input  s5,
  output O
);

  wire and_1_out, and_2_out, and_3_out, and_4_out, and_5_out, and_6_out, and_7_out, and_8_out, and_9_out,
       not_1_out, not_2_out, not_3_out, not_4_out, not_5_out, not_6_out;

  not not_1 (not_1_out, s0);
  not not_2 (not_2_out, s1);
  not not_3 (not_3_out, s2);
  not not_4 (not_4_out, s3);
  not not_5 (not_5_out, s4);
  not not_6 (not_6_out, s5);
  and and_1 (and_1_out, not_1_out, not_2_out, not_3_out, s4);
  and and_2 (and_2_out, not_3_out, s4, not_6_out);
  and and_3 (and_3_out, s2, s3, s4, s5);
  and and_4 (and_4_out, s1, not_3_out, not_4_out);
  and and_5 (and_5_out, s1, not_3_out, not_5_out);
  and and_6 (and_6_out, s1, not_3_out, not_6_out);
  and and_7 (and_7_out, s0, not_3_out, not_4_out);
  and and_8 (and_8_out, s0, not_3_out, not_5_out);
  and and_9 (and_9_out, s0, not_3_out, not_6_out);
  or or_1 (O, and_1_out, and_2_out, and_3_out, and_4_out, and_5_out, and_6_out, and_7_out, and_8_out, and_9_out);
endmodule

module C3 (
  input  s0,
  input  s1,
  input  s2,
  input  s3,
  input  s4,
  input  s5,
  output O
);

  wire and_1_out, and_2_out, and_3_out, and_4_out, and_5_out, and_6_out, and_7_out, not_1_out, not_2_out,
       not_3_out, not_4_out, not_5_out, not_6_out;

  not not_1 (not_1_out, s0);
  not not_2 (not_2_out, s1);
  not not_3 (not_3_out, s2);
  not not_4 (not_4_out, s3);
  not not_5 (not_5_out, s4);
  not not_6 (not_6_out, s5);
  and and_1 (and_1_out, not_1_out, not_2_out, not_3_out, s5);
  and and_2 (and_2_out, not_1_out, not_2_out, not_5_out, s5);
  and and_3 (and_3_out, not_4_out, s4, s5);
  and and_4 (and_4_out, s3, not_5_out, s5);
  and and_5 (and_5_out, s2, s3, not_6_out);
  and and_6 (and_6_out, s1, s3, not_6_out);
  and and_7 (and_7_out, s0, s3, not_6_out);
  or or_1 (O, and_1_out, and_2_out, and_3_out, and_4_out, and_5_out, and_6_out, and_7_out);
endmodule

module LESelector (
  input  LE0,
  input  LE1,
  output RED,
  output YELLOW,
  output GREEN
);

  and and_1 (RED, LE0, ~LE1);  // AND_Gate
  and and_2 (YELLOW, ~LE0, LE1);  // AND_Gate
  nor nor_1 (GREEN, LE0, LE1);
endmodule

module LXSelector (
  input  LX0,
  input  LX1,
  output RED,
  output YELLOW,
  output GREEN
);

  and and_1 (RED, LX0, ~LX1);  // AND_Gate
  and and_2 (YELLOW, ~LX0, LX1);  // AND_Gate
  nor nor_1 (GREEN, LX0, LX1);
endmodule

module SevenSeg (
  input  C_0,
  input  C_1,
  input  C_2,
  input  C_3,
  output A,
  output B,
  output C,
  output D,
  output E,
  output F,
  output G
);

  wire and_1_out, and_2_out, and_3_out, and_4_out, and_5_out, and_6_out, and_7_out, and_8_out, and_9_out,
       and_10_out, and_11_out, and_12_out, and_13_out, and_14_out, and_15_out, and_16_out, and_17_out,
       and_18_out, and_19_out, and_20_out, and_21_out, and_22_out, and_23_out, and_24_out, and_25_out,
       and_26_out, not_1_out, not_2_out, not_3_out, not_4_out;

  not not_1 (not_1_out, C_3);
  not not_2 (not_2_out, C_2);
  not not_3 (not_3_out, C_1);
  not not_4 (not_4_out, C_0);
  and and_1 (and_1_out, not_1_out, C_1);
  and and_2 (and_2_out, not_1_out, C_2, C_0);
  and and_3 (and_3_out, C_3, not_2_out, not_3_out);
  and and_4 (and_4_out, not_2_out, not_3_out, not_4_out);
  and and_5 (and_5_out, not_1_out, not_2_out);
  and and_6 (and_6_out, not_2_out, not_3_out);
  and and_7 (and_7_out, not_1_out, C_1, C_0);
  and and_8 (and_8_out, not_1_out, not_3_out, not_4_out);
  and and_9 (and_9_out, not_2_out, not_3_out);
  and and_10 (and_10_out, not_1_out, C_2);
  and and_11 (and_11_out, not_1_out, C_0);
  and and_12 (and_12_out, not_2_out, not_3_out, not_4_out);
  and and_13 (and_13_out, not_1_out, not_2_out, C_1);
  and and_14 (and_14_out, not_1_out, C_1, not_4_out);
  and and_15 (and_15_out, C_3, not_2_out, not_3_out);
  and and_16 (and_16_out, not_1_out, C_2, not_3_out, C_0);
  and and_17 (and_17_out, not_2_out, not_3_out, not_4_out);
  and and_18 (and_18_out, not_1_out, C_1, not_4_out);
  and and_19 (and_19_out, not_2_out, not_3_out, not_4_out);
  and and_20 (and_20_out, not_1_out, C_2, not_3_out);
  and and_21 (and_21_out, not_1_out, C_2, not_4_out);
  and and_22 (and_22_out, C_3, not_2_out, not_3_out);
  and and_23 (and_23_out, not_1_out, not_2_out, C_1);
  and and_24 (and_24_out, not_1_out, C_2, not_3_out);
  and and_25 (and_25_out, not_1_out, C_1, not_4_out);
  and and_26 (and_26_out, C_3, not_2_out, not_3_out);
  or or_1 (A, and_1_out, and_2_out, and_3_out, and_4_out);
  or or_2 (B, and_5_out, and_6_out, and_7_out, and_8_out);
  or or_3 (C, and_9_out, and_10_out, and_11_out);
  or or_4 (D, and_12_out, and_13_out, and_14_out, and_15_out, and_16_out);
  or or_5 (E, and_17_out, and_18_out);
  or or_6 (F, and_19_out, and_20_out, and_21_out, and_22_out);
  or or_7 (G, and_23_out, and_24_out, and_25_out, and_26_out);
endmodule
